// Logisim project demux_4_1.circ as structural Verilog: 1 circuit, main circuit main
module main (
);

  wire and_1_out, and_2_out, and_3_out, and_4_out, clock_1_out, not_1_out, not_2_out;

  Clock clock_1 (.out(clock_1_out));
  not not_1 (not_1_out, 1'b0);
  not not_2 (not_2_out, 1'b0);
  and and_1 (and_1_out, clock_1_out, not_1_out, not_2_out);
  and and_2 (and_2_out, clock_1_out, not_1_out, 1'b0);
  and and_3 (and_3_out, clock_1_out, 1'b0, not_2_out);
  and and_4 (and_4_out, clock_1_out, 1'b0, 1'b0);
endmodule
